// Digital circuit Lab2.dig as structural Verilog
module Lab2 (
  input  I3,
  input  I2,
  input  I1,
  input  I0,
  output Q0,
  output Q1,
  output Q2,
  output Q3,
  output Q4,
  output Q5
);

  wire and_1_out, and_2_out, not_1_out, not_2_out;

  not not_1 (not_1_out, I3);
  not not_2 (not_2_out, I1);
  and and_1 (and_1_out, I0, not_1_out);
  and and_2 (and_2_out, I1, not_1_out);
  and and_3 (Q2, not_2_out, not_1_out);
  and and_4 (Q3, I0, not_1_out);
  and and_5 (Q4, I2, not_1_out);
  or or_1 (Q1, and_1_out, and_2_out);

  assign Q0 = I0;
  assign Q5 = I3;
endmodule
