// Digital circuit Lab2Digital.dig as structural Verilog
module Lab2Digital (
  input  I3,
  input  I2,
  input  I1,
  input  I0,
  output Q0,
  output Q1,
  output Q2,
  output Q3,
  output Q4
);

  wire and_1_out, and_2_out, not_1_out;

  not not_1 (not_1_out, I3);
  not not_2 (Q2, I1);
  not not_3 (Q0, I0);
  and and_1 (and_1_out, I0, not_1_out);
  and and_2 (and_2_out, I1, not_1_out);
  or or_1 (Q1, and_1_out, and_2_out);

  assign Q3 = I2;
  assign Q4 = I3;
endmodule
